# Fritzing sketch main (saved by Fritzing 0.9.3b)
perfboards: 1

parts:
  Q1 = NPN-Transistor [package="TO92 [THT]"]
  Q3 = NPN-Transistor [package="TO92 [THT]"]
  C1 = Ceramic Capacitor [capacitance="100 nF" package="0805 [SMD, multilayer]"]
  C3 = Electrolytic Capacitor [package="2cm H-Type"]
  C4 = Electrolytic Capacitor [package="2cm H-Type"]
  R1 = Resistor [tolerance=±5% resistance=510 package="0805 [SMD]"]
  M1 = DC Motor
  IC1 = Voltage Regulator [package=to-92]
  Part1 = Soil Moisture Sensor
  Solar_Cell1 = 5V 100mA Polycrystalline PET Solar Cell [part_number=IM130407002]
  Part2 = Power Cell LiPo Charger/Booster
  R8 = Resistor [tolerance=±1% resistance=10 package="2512 [SMD]"]
  USBTTL1 = USB TTL Serial Cable
  BAT1 = Battery Holders [package=lipo-1100mAh]
  R7 = Resistor [tolerance=±1% resistance=10k package="0805 [SMD]"]
  R2 = Resistor [tolerance=±5% resistance=3.3k package="0805 [SMD]"]
  U1 = ATTINY13 [package=dip]

nets (from the schematic view):
  GND: Q1.E, Q3.E, R8.Pin_0
  N1: Q1.B, R2.Pin_0
  N2: Q1.C, IC1.IN
  N3: Q3.B, R1.Pin_1, R8.Pin_1
  N4: Q3.C, M1.pin_2
  VCC: C1.0, M1.pin_1, Part2.VCC, U1.VCC
  N5: C1.1, R7.Pin_1, U1.GND
  N6: C3.-, C4.-, Solar_Cell1.GND
  N7: C3.+, IC1.GND
  N8: C4.+, Solar_Cell1.5V
  N9: R1.Pin_0, U1.PB0(MOSI)
  N10: IC1.OUT, Part2.5VIN
  N11: Part1.VCC, U1.PB1(MISO)
  N12: Part1.SIG, R7.Pin_0, U1.PB4(ADC2)
  N13: Part2.GND, BAT1.-
  N14: Part2.PS, BAT1.+
  N15: USBTTL1.RX, U1.PB3(ADC3)
  N16: R2.Pin_1, U1.PB2(SCK_ADC1)

notes:
  TX
  78l05
  5V
  104
  USB Serial
  Pump DC Motor
  Moisture Sensor
  A0
  Lithium-ion Battery
  Lithium-ion Charger with Protection
  NPN
  510R
  10K
  3.3K

custom parts:
  5V 100mA Polycrystalline PET Solar Cell: This is 5V 100mA Polycrystalline PET Solar Cell. It is high quality and exquisite appearance. It is used in all kinds of high-grade electronic products.
